# Fritzing sketch ESP8266-DHT11-ThingSpeak (saved by Fritzing 0.9.3b)
breadboards: 1

parts:
  AMS1117 = Voltage Regulator - 3.3V [package="TO220 [THT]"]
  DHT11 = Humidity and Temperature Sensor RHT03
  C3 = Electrolytic Capacitor [capacitance=100μF voltage=50V package="0807 [SMD, electrolytic]"]
  VCC1 = Battery block 9V
  0_1uF = Capacitor [package=cap-pth-small]
  U1 = ESP8266 WiFi Module [part_number=ESP8266]

nets:
  N1: AMS1117.input_voltage, VCC1.+, 0_1uF.1
  GND: AMS1117.GND, DHT11.GND_2, C3.-, VCC1.-, 0_1uF.2, U1.GND
  VCC: AMS1117.output_voltage, DHT11.Vcc, C3.+, U1.VCC, U1.CH_PD
  N2: DHT11.Data-signal, U1.GPIO_2

notes:
  NOTE: some DHT11 modules should add a pull-up resistor in Data pin (2nd left to right)

custom parts:
  ESP8266 WiFi Module: Generic WiFi Module based on the ESP8266 with onboard PCB antenna and UART communications
